# Fritzing sketch PIRServoUNO5V (saved by Fritzing 0.9.2b)

parts:
  J1 = Basic Servo
  PIR2 = PIR sensor
  Part1 = Arduino Uno (Rev3) - ICSP
  5V_power = Power plug

nets:
  GND: J1.gnd, PIR2.GND, Part1.GND, 5V_power.GND
  VCC: J1.vcc, PIR2.VCC, Part1.5V, 5V_power.VCC
  N1: J1.pulse, Part1.D6_PWM
  N2: PIR2.SIG, Part1.D4
